# Fritzing sketch digital_input (saved by Fritzing 0.9.4)
breadboards: 1

parts:
  Arduino2 = Arduino Uno (Rev3)
  Switch = Pushbutton [package=THT]
  Resistor = Resistor [tolerance=±5% resistance=10k package=THT]
  S1 = Pushbutton [package="[THT]"]
  Resistor1 = Resistor [tolerance=±5% resistance=10k package=THT]

nets:
  N1: Arduino2.GND, Resistor.Pin_1, Resistor1.Pin_1
  N2: Arduino2.D2, Switch.leg0, Resistor.Pin_0, S1.Pin_1, S1.Pin_2, Resistor1.Pin_0
  N3: Arduino2.5V, Switch.leg1, S1.Pin_3, S1.Pin_4

notes:
  --- OR ----
