# Fritzing sketch digital_output (saved by Fritzing 0.9.4)
breadboards: 1

parts:
  Part1 = Arduino Uno (Rev3)
  LED = LED - 5mm [color="Red (633nm)" package="5 mm [THT]"]
  R = Resistor [tolerance=±5% resistance=220 package=THT]

nets:
  N1: Part1.D13/SCK, R.Pin_1
  N2: Part1.GND, LED.cathode
  N3: LED.anode, R.Pin_0
