# Fritzing sketch digital_output2 (saved by Fritzing 0.9.4)

parts:
  Part1 = Arduino Uno (Rev3)
  Mod1 = KY-019 5V Relay Module [package="Breakout board"]

nets:
  N1: Part1.D13/SCK, Mod1.S
  N2: Part1.5V, Mod1.+
  N3: Part1.GND, Mod1.-

custom parts:
  KY-019 5V Relay Module: KY-019 5V Relay module, used to control AC circuits. (Special thanks to vanepp for fixing the PCB holes and other errors)
