# Fritzing sketch analogInLDR (saved by Fritzing 1.0.6)
breadboards: 1

parts:
  Part1 = Arduino Uno (Rev3)
  LED = LED - 5mm [color="Red (633nm)" current=0.030A package="5 mm [THT]"]
  part = Resistor [tolerance=±5% resistance=220 power=0.25W package=THT]
  LDR = Photocell (LDR) [power=0.25W dark_resistance_@0.01lx=300kΩ light_resistance_@100lx=400Ω luminance=10lx package=THT]
  part_2 = Resistor [tolerance=±5% power=0.25W resistance=10k package=THT]

nets:
  N1: Part1.A0, LDR.pin_1, part_2.Pin_0
  N2: Part1.D2, part.Pin_1
  N3: Part1.5V, LDR.pin_0
  N4: Part1.GND, LED.cathode, part_2.Pin_1
  N5: LED.anode, part.Pin_0
